# Fritzing sketch rc-receiver-backpack-edison-arduino (saved by Fritzing 0.9.1b)

parts:
  Part1 = Arduino Nano (Rev3.0) (ICSP)
  ANT1 = Antenna
  Part2 = Intel Edison Arduinobreakout

nets:
  GND: Part1.GND, ANT1.GND, Part2.GND
  N1: Part1.D2, ANT1.C1
  N2: Part1.D3, ANT1.C2
  N3: Part1.D4, ANT1.C3
  N4: Part1.D5, ANT1.C4
  N5: Part1.D6, ANT1.C5
  N6: Part1.D7, ANT1.C6
  N7: Part1.D8, ANT1.C7
  N8: Part1.D9, ANT1.C8
  VIN: Part1.VIN, Part2.5V
  5V: Part1.5V, ANT1.VCC
  N9: Part1.A5, Part2.A5/SCL
  N10: Part1.A4, Part2.A4/SDA

custom parts:
  Antenna: Random Wire Antenna
