# Fritzing sketch rc-receiver-backpack-rpi-mini (saved by Fritzing 0.9.1b)

parts:
  ANT1 = Antenna
  Part2 = Arduino Pro Mini v13
  Raspberry_Pi_B_rev2 = Raspberry Pi B+

nets:
  GND: ANT1.GND, Part2.GND, Raspberry_Pi_B_rev2.GND
  VCC: ANT1.VCC, Part2.VCC, Raspberry_Pi_B_rev2.3v3
  N1: ANT1.C1, Part2.D2
  N2: ANT1.C2, Part2.D3_PWM
  N3: ANT1.C3, Part2.D4
  N4: ANT1.C4, Part2.D5_PWM
  N5: ANT1.C5, Part2.D6_PWM
  N6: ANT1.C6, Part2.D7
  N7: ANT1.C7, Part2.D8
  N8: ANT1.C8, Part2.D9_PWM
  N9: Part2.A4, Raspberry_Pi_B_rev2.GPIO2
  N10: Part2.A5, Raspberry_Pi_B_rev2.GPIO3

custom parts:
  Antenna: Random Wire Antenna
