# Fritzing sketch rc-receiver-backpack-tessel-mini (saved by Fritzing 0.9.1b)

parts:
  ANT1 = Antenna
  Part2 = Arduino Pro Mini v13
  Part4 = Tessel 2

nets:
  GND: ANT1.GND, Part2.GND, Part4.GND
  VCC: ANT1.VCC, Part2.VCC, Part4.3V3
  N1: ANT1.C1, Part2.D2
  N2: ANT1.C2, Part2.D3_PWM
  N3: ANT1.C3, Part2.D4
  N4: ANT1.C4, Part2.D5_PWM
  N5: ANT1.C5, Part2.D6_PWM
  N6: ANT1.C6, Part2.D7
  N7: ANT1.C7, Part2.D8
  N8: ANT1.C8, Part2.D9_PWM
  N9: Part2.A4, Part4.1
  N10: Part2.A5, Part4.0

custom parts:
  Antenna: Random Wire Antenna
  Tessel 2: Draft version of Tessel 2
